# Fritzing sketch frescobol-nano-bt (saved by Fritzing 0.9.3b)
circuit board: 4.82619cm x 5.90788cm

parts:
  S1 = Momentary Switch [package=ksa_sealed_tac_switch]
  S2 = Momentary Switch [package=ksa_sealed_tac_switch]
  TP1 = TP4056 [chip_label=TP4056 package="DIP (Dual Inline) [THT]"]
  Part5 = Bluetooth HC-05 Macho
  S3 = Momentary Switch [package=ksa_sealed_tac_switch]
  SW1 = DIP SWITCH [package=dipswitch-02]
  J2 = male pin header, 1 pin [form="♂ (male)"]
  J3 = male pin header, 1 pin [form="♂ (male)"]
  J4 = male pin header, 1 pin [form="♂ (male)"]
  J5 = male pin header, 1 pin [form="♂ (male)"]
  J6 = male pin header, 1 pin [form="♂ (male)"]
  J7 = male pin header, 1 pin [form="♂ (male)"]
  J8 = male pin header, 1 pin [form="♂ (male)"]
  J9 = male pin header, 1 pin [form="♂ (male)"]
  R1 = Resistor [tolerance=±5% resistance=2.2k package=THT]
  R2 = Resistor [tolerance=±5% resistance=1k package=THT]
  Part4 = Arduino Nano (Rev3.0) (ICSP)
  J10 = male pin header, 1 pin [form="♂ (male)"]
  J11 = male pin header, 1 pin [form="♂ (male)"]
  J12 = male pin header, 1 pin [form="♂ (male)"]
  J13 = male pin header, 1 pin [form="♂ (male)"]

nets:
  N1: S1.2, J6.pin1, Part4.D3, J12.pin1
  N2: S1.3, J5.pin1
  N3: S1.4, S2.3, TP1.pin5, J7.pin1, J13.pin1
  N4: S2.2, J8.pin1, Part4.D2, J10.pin1
  GND: S2.4, Part5.GND, S3.1, J3.pin1, J9.pin1, R1.Pin_0, Part4.GND, J11.pin1
  N5: TP1.pin4, SW1.3, J2.pin1
  N6: Part5.TXD, Part4.D0/RX
  N7: Part5.RXD, R1.Pin_1, R2.Pin_1
  N8: Part5.VCC, SW1.4
  N9: S3.4, Part4.D4
  N10: SW1.1, SW1.2, Part4.5V
  N11: J4.pin1, Part4.D11/MOSI
  N12: R2.Pin_0, Part4.D1/TX

custom parts:
  TP4056: A DIP stand-in part for whatever IC you want. With 6 pins on a 300mil dual inline package (DIP) footprint.
